// Logisim project 实验01_Logism入门.circ as structural Verilog: 9 circuits, main circuit main
module main (
  input  a,
  input  b,
  input  c,
  input  d,
  input  sel1,
  input  sel0,
  input  in_7,
  input  [3:0] in_8,
  input  [7:0] in_9,
  output out,
  output out_11,
  output [3:0] out_12,
  output [3:0] out_13,
  output [5:0] out_14,
  output [3:0] out_15,
  output [3:0] out_16,
  output [1:0] out_17,
  output [3:0] out_18,
  output [1:0] out_19,
  output [1:0] out_20,
  output [1:0] out_21,
  output [1:0] out_22
);

  wire button_1_out;

  BitSelector #(.width(4)) bitselector_1 (.in({d, c, b, a}), .out(out), .sel({sel1, sel0}));
  Button button_1 (.out(button_1_out));
  // Probe on in_8
  // Probe on in_8
  // Probe on in_8
  // Probe on in_8
  LED led_1 (.in(button_1_out));
  // Probe on in_8

  assign out_11 = in_7;
  assign out_12 = in_8;
  assign out_13 = in_9[7:4];
  assign out_14 = in_9[7:2];
  assign out_15 = in_9[3:0];
  assign out_16 = in_9[3:0];
  assign out_17 = in_9[1:0];
  assign out_18 = in_9[7:4];
  assign out_19 = in_9[1:0];
  assign out_20 = in_9[3:2];
  assign out_21 = in_9[5:4];
  assign out_22 = in_9[7:6];
endmodule

module Name (
);

  DotMatrix #(.matrixcols(28)) dotmatrix_1 (
    .col0(7'b0001010), .col1(7'b0010101), .col2(7'b0010101), .col3({7{1'b0}}), .col4(7'b0010011),
    .col5(7'b0010101), .col6(7'b0011001), .col7({7{1'b0}}), .col8(7'b0001010), .col9(7'b0010101),
    .col10(7'b0010101), .col11({7{1'b0}}), .col12({7{1'b1}}), .col13(7'b0000100), .col14(7'b0001010),
    .col15(7'b0010001), .col16({7{1'b0}}), .col17(7'b0010001), .col18(7'b0011111), .col19(7'b0010001),
    .col20({7{1'b0}}), .col21(7'b0001010), .col22(7'b0010101), .col23(7'b0010101), .col24({7{1'b0}}),
    .col25({7{1'b1}}), .col26(7'b0000001), .col27(7'b0000001));

  // Notes on the sheet:
  //   OUEDRAOGO EZEKIEL B.
  //   PL19215001
endmodule

module studentID (
);

  _7_Segment_Display u_7_segment_display_1 (
    .g(1'b1), .f(1'b1), .a(1'b1), .b(1'b1), .e(1'b1), .d(1'b0), .c(1'b0), .dp(1'b0));
  _7_Segment_Display u_7_segment_display_2 (
    .g(1'b0), .f(1'b1), .a(1'b0), .b(1'b0), .e(1'b1), .d(1'b1), .c(1'b0), .dp(1'b0));
  _7_Segment_Display u_7_segment_display_3 (
    .g(1'b0), .f(1'b0), .a(1'b0), .b(1'b1), .e(1'b0), .d(1'b0), .c(1'b1), .dp(1'b0));
  _7_Segment_Display u_7_segment_display_4 (
    .g(1'b1), .f(1'b1), .a(1'b1), .b(1'b1), .e(1'b0), .d(1'b1), .c(1'b1), .dp(1'b0));
  _7_Segment_Display u_7_segment_display_5 (
    .g(1'b1), .f(1'b0), .a(1'b1), .b(1'b1), .e(1'b1), .d(1'b1), .c(1'b0), .dp(1'b0));
  _7_Segment_Display u_7_segment_display_6 (
    .g(1'b0), .f(1'b0), .a(1'b0), .b(1'b1), .e(1'b0), .d(1'b0), .c(1'b1), .dp(1'b0));
  _7_Segment_Display u_7_segment_display_7 (
    .g(1'b1), .f(1'b1), .a(1'b1), .b(1'b0), .e(1'b0), .d(1'b1), .c(1'b1), .dp(1'b0));
  _7_Segment_Display u_7_segment_display_8 (
    .g(1'b0), .f(1'b1), .a(1'b1), .b(1'b1), .e(1'b1), .d(1'b1), .c(1'b1), .dp(1'b0));
  _7_Segment_Display u_7_segment_display_9 (
    .g(1'b0), .f(1'b1), .a(1'b1), .b(1'b1), .e(1'b1), .d(1'b1), .c(1'b1), .dp(1'b0));
  _7_Segment_Display u_7_segment_display_10 (
    .g(1'b0), .f(1'b0), .a(1'b0), .b(1'b1), .e(1'b0), .d(1'b0), .c(1'b1), .dp(1'b0));

  // Notes on the sheet:
  //   PL19215001
  //   OUEDRAOGO EZEKIEL B.
endmodule

module And_OR_NOT (
  input  in_1,
  input  in_2,
  input  in_3,
  input  in_4,
  input  in_5,
  output out_6,
  output out_7,
  output out_8
);

  wire transistor_2_out, transistor_7_out;

  Transistor transistor_1 (.in(1'b0), .out(out_8), .gate(in_4));
  Transistor #(.\type ("n")) transistor_2 (.in(1'b1), .out(transistor_2_out), .gate(in_2));
  Transistor #(.\type ("n")) transistor_3 (.in(transistor_2_out), .out(out_8), .gate(in_4));
  Transistor transistor_4 (.in(1'b0), .out(out_8), .gate(in_2));
  Transistor #(.\type ("n")) transistor_5 (.in(1'b1), .out(out_6), .gate(in_1));
  Transistor transistor_6 (.in(transistor_7_out), .out(out_6), .gate(in_5));
  Transistor transistor_7 (.in(1'b0), .out(transistor_7_out), .gate(in_1));
  Transistor #(.\type ("n")) transistor_8 (.in(1'b1), .out(out_6), .gate(in_5));
  Transistor transistor_9 (.in(1'b1), .out(out_7), .gate(in_3));
  Transistor #(.\type ("n")) transistor_10 (.in(1'b0), .out(out_7), .gate(in_3));

  // Notes on the sheet:
  //   OUEDRAOGO EZEKIEL B.
  //   PL19215001
  //   AND Gate
  //   OR Gate
  //   Not Gate
endmodule

module AND (
  input  in_1,
  input  in_2,
  output out_3
);

  wire transistor_2_out;

  Transistor transistor_1 (.in(1'b0), .out(out_3), .gate(in_2));
  Transistor #(.\type ("n")) transistor_2 (.in(1'b1), .out(transistor_2_out), .gate(in_1));
  Transistor #(.\type ("n")) transistor_3 (.in(transistor_2_out), .out(out_3), .gate(in_2));
  Transistor transistor_4 (.in(1'b0), .out(out_3), .gate(in_1));

  // Notes on the sheet:
  //   PL19215001
  //   OUEDRAOGO EZEKIEL B.
endmodule

module OR (
  input  in_1,
  input  in_2,
  output out_3
);

  wire transistor_3_out;

  Transistor #(.\type ("n")) transistor_1 (.in(1'b1), .out(out_3), .gate(in_1));
  Transistor transistor_2 (.in(transistor_3_out), .out(out_3), .gate(in_2));
  Transistor transistor_3 (.in(1'b0), .out(transistor_3_out), .gate(in_1));
  Transistor #(.\type ("n")) transistor_4 (.in(1'b1), .out(out_3), .gate(in_2));

  // Notes on the sheet:
  //   OUEDRAOGO EZEKIEL B.
  //   PL19215001
endmodule

module NOT (
  input  in_1,
  output out_2
);

  Transistor transistor_1 (.in(1'b1), .out(out_2), .gate(in_1));
  Transistor #(.\type ("n")) transistor_2 (.in(1'b0), .out(out_2), .gate(in_1));

  // Notes on the sheet:
  //   OUEDRAOGO EZEKIEL B.
  //   PL19215001
endmodule

module MUX_2 (
  input  a,
  input  b,
  input  sel,
  output out
);

  wire and_1_out_3, and_2_out_3, not_1_out_2;

  NOT not_1 (.in_1(sel), .out_2(not_1_out_2));
  AND and_1 (.in_1(b), .in_2(sel), .out_3(and_1_out_3));
  AND and_2 (.in_1(a), .in_2(not_1_out_2), .out_3(and_2_out_3));
  OR or_1 (.in_1(and_1_out_3), .in_2(and_2_out_3), .out_3(out));

  // Notes on the sheet:
  //   OUEDRAOGO EZEKIEL B.
  //   PL19215001
endmodule

module MUX_4 (
  input  sel1,
  input  sel0,
  input  [1:0] a,
  input  [1:0] b,
  input  [1:0] c,
  input  [1:0] d,
  output [1:0] out
);

  wire mux_2_1_out, mux_2_2_out, mux_2_3_out, mux_2_4_out;

  MUX_2 mux_2_1 (.a(a[0]), .b(b[0]), .sel(sel0), .out(mux_2_1_out));
  MUX_2 mux_2_2 (.a(a[1]), .b(b[1]), .sel(sel1), .out(mux_2_2_out));
  MUX_2 mux_2_3 (.a(c[0]), .b(d[0]), .sel(sel0), .out(mux_2_3_out));
  MUX_2 mux_2_4 (.a(c[1]), .b(d[1]), .sel(sel1), .out(mux_2_4_out));
  MUX_2 mux_2_5 (.a(mux_2_1_out), .b(mux_2_3_out), .sel(sel0), .out(out[0]));
  MUX_2 mux_2_6 (.a(mux_2_2_out), .b(mux_2_4_out), .sel(sel1), .out(out[1]));

  // Notes on the sheet:
  //   PL19215001
  //   OUEDRAOGO EZEKIEL B.
endmodule
