// Logisim project 实验02_简单组合逻辑电路.circ as structural Verilog
module truth_table (
  input  Ci1,
  input  Ai,
  input  Bi,
  output Si,
  output Ci
);

  wire and_1_out, and_2_out, and_3_out, and_4_out, and_5_out, and_6_out, and_7_out, not_1_out, not_2_out,
       not_3_out, not_4_out, not_5_out, not_6_out;

  not not_1 (not_1_out, Ci1);
  not not_2 (not_2_out, Ai);
  not not_3 (not_3_out, Ci1);
  not not_4 (not_4_out, Bi);
  not not_5 (not_5_out, Ai);
  not not_6 (not_6_out, Bi);
  and and_1 (and_1_out, Ai, Bi);
  and and_2 (and_2_out, Ci1, Bi);
  and and_3 (and_3_out, Ci1, Ai);
  and and_4 (and_4_out, not_1_out, not_2_out, Bi);
  and and_5 (and_5_out, not_3_out, Ai, not_4_out);
  and and_6 (and_6_out, Ci1, not_5_out, not_6_out);
  and and_7 (and_7_out, Ci1, Ai, Bi);
  or or_1 (Ci, and_1_out, and_2_out, and_3_out);
  or or_2 (Si, and_4_out, and_5_out, and_6_out, and_7_out);

  // Notes on the sheet:
  //   PL19215001
  //   OUEDRAOGO EZEKIEL B.
endmodule

module Function (
  input  G1,
  input  G2,
  input  G3,
  input  A2,
  input  A1,
  input  A0,
  output Y7,
  output Y6,
  output Y5,
  output Y4,
  output Y3,
  output Y2,
  output Y1,
  output Y0
);

  wire not_1_out, not_2_out, not_3_out, not_4_out, not_5_out, not_6_out, not_7_out, not_8_out, not_9_out,
       not_10_out, not_11_out, not_12_out, not_13_out, not_14_out, not_15_out, not_16_out, not_17_out,
       not_18_out, not_19_out, not_20_out;

  not not_1 (not_1_out, G1);
  not not_2 (not_2_out, A2);
  not not_3 (not_3_out, A1);
  not not_4 (not_4_out, A0);
  not not_5 (not_5_out, G1);
  not not_6 (not_6_out, A2);
  not not_7 (not_7_out, A1);
  not not_8 (not_8_out, G1);
  not not_9 (not_9_out, A2);
  not not_10 (not_10_out, A0);
  not not_11 (not_11_out, G1);
  not not_12 (not_12_out, A2);
  not not_13 (not_13_out, G1);
  not not_14 (not_14_out, A1);
  not not_15 (not_15_out, A0);
  not not_16 (not_16_out, G1);
  not not_17 (not_17_out, A1);
  not not_18 (not_18_out, G1);
  not not_19 (not_19_out, A0);
  not not_20 (not_20_out, G1);
  or or_1 (Y7, not_1_out, G2, G3, not_2_out, not_3_out, not_4_out);
  or or_2 (Y6, not_5_out, G2, G3, not_6_out, not_7_out, A0);
  or or_3 (Y5, not_8_out, G2, G3, not_9_out, A1, not_10_out);
  or or_4 (Y4, not_11_out, G2, G3, not_12_out, A1, A0);
  or or_5 (Y3, not_13_out, G2, G3, A2, not_14_out, not_15_out);
  or or_6 (Y2, not_16_out, G2, G3, A2, not_17_out, A0);
  or or_7 (Y1, not_18_out, G2, G3, A2, A1, not_19_out);
  or or_8 (Y0, not_20_out, G2, G3, A2, A1, A0);

  // Notes on the sheet:
  //   OUEDRAOGO EZEKIEL B.
  //   PL19215001
endmodule

module MUX_2 (
  input  a,
  input  b,
  input  sel,
  output out
);

  wire and_1_out, and_2_out, not_1_out;

  not not_1 (not_1_out, sel);
  and and_1 (and_1_out, b, sel);
  and and_2 (and_2_out, a, not_1_out);
  or or_1 (out, and_1_out, and_2_out);

  // Notes on the sheet:
  //   PL19215001
  //   OUEDRAOGO EZEKIEL B.
endmodule

module MUX_4 (
  input  a,
  input  b,
  input  c,
  input  d,
  input  sel1,
  input  sel0,
  output out
);

  wire mux1_out, mux2_out;

  MUX_2 mux1 (.a(a), .b(c), .sel(sel1), .out(mux1_out));
  MUX_2 mux2 (.a(b), .b(d), .sel(sel1), .out(mux2_out));
  MUX_2 mux3 (.a(mux1_out), .b(mux2_out), .sel(sel0), .out(out));

  // Notes on the sheet:
  //   w1
  //   w2
  //   OUEDRAOGO EZEKIEL B.
  //   PL19215001
endmodule

module encoder (
  input  i7,
  input  i6,
  input  i5,
  input  i4,
  input  i3,
  input  i2,
  input  i1,
  input  i0,
  output y2,
  output y1,
  output y0
);

  wire not_1_out, not_2_out, not_3_out, not_4_out, not_5_out, or_2_out, or_3_out, or_4_out, or_5_out,
       or_6_out, or_7_out, or_8_out;

  or or_1 (y2, i7, i6, i5, i4);
  or or_2 (or_2_out, i7, i6, i3, i2);
  or or_3 (or_3_out, i7, i6, not_1_out);
  not not_1 (not_1_out, i4);
  or or_4 (or_4_out, i7, i6, not_2_out);
  not not_2 (not_2_out, i5);
  not not_3 (not_3_out, i2);
  not not_4 (not_4_out, i4);
  not not_5 (not_5_out, i6);
  and and_1 (y1, or_2_out, or_3_out, or_4_out);
  or or_5 (or_5_out, i7, i5, i3, i1);
  or or_6 (or_6_out, i7, i5, i3, not_3_out);
  or or_7 (or_7_out, i7, i5, not_4_out);
  or or_8 (or_8_out, i7, not_5_out);
  and and_2 (y0, or_5_out, or_6_out, or_7_out, or_8_out);

  // Notes on the sheet:
  //   PL19215001
  //   OUEDRAOGO EZEKIEL B.
endmodule

module unknown (
  input  a,
  input  b,
  input  c,
  output S1,
  output S2
);

  wire and_1_out, and_2_out, and_3_out, and_4_out, and_5_out, and_6_out, and_7_out, and_8_out, not_1_out,
       not_2_out, not_3_out, not_4_out, not_5_out, not_6_out, not_7_out, not_8_out, not_9_out, not_10_out,
       not_11_out, not_12_out;

  not not_1 (not_1_out, a);
  not not_2 (not_2_out, b);
  not not_3 (not_3_out, a);
  not not_4 (not_4_out, c);
  not not_5 (not_5_out, b);
  not not_6 (not_6_out, c);
  not not_7 (not_7_out, a);
  not not_8 (not_8_out, b);
  not not_9 (not_9_out, c);
  not not_10 (not_10_out, a);
  not not_11 (not_11_out, b);
  not not_12 (not_12_out, c);
  and and_1 (and_1_out, not_1_out, not_2_out, c);
  and and_2 (and_2_out, not_3_out, b, not_4_out);
  and and_3 (and_3_out, a, not_5_out, not_6_out);
  and and_4 (and_4_out, a, b, c);
  and and_5 (and_5_out, not_7_out, not_8_out, not_9_out);
  and and_6 (and_6_out, not_10_out, b, c);
  and and_7 (and_7_out, a, not_11_out, c);
  and and_8 (and_8_out, a, b, not_12_out);
  or or_1 (S1, and_1_out, and_2_out, and_3_out, and_4_out);
  or or_2 (S2, and_5_out, and_6_out, and_7_out, and_8_out);

  // Notes on the sheet:
  //   OUEDRAOGO EZEKIEL B.
  //   PL19215001
endmodule
