// Logisim project 实验03_简单时序逻辑电路.circ as structural Verilog: 16 circuits, main circuit main
module main (
  input  nST,
  input  nS,
  input  D,
  input  D_2,
  input  nRST,
  input  nRST_2,
  input  nR,
  input  D_3,
  input  nRST_3,
  input  D_4,
  input  D_5,
  input  D_6,
  input  RST,
  input  RST_2,
  input  D_7,
  input  D_8,
  input  ST,
  input  [3:0] IN,
  input  [3:0] Reset_Value,
  input  nR_2,
  input  D_9,
  input  nRST_4,
  input  [3:0] IN_2,
  input  nR_3,
  output Q,
  output Q_2,
  output Q_3,
  output nQ,
  output nQ_2,
  output nQ_3,
  output Q_4,
  output nQ_4,
  output Q_5,
  output Q_6,
  output Q_7,
  output nQ_5,
  output nQ_6,
  output nQ_7,
  output [3:0] OUT,
  output Q_8,
  output nQ_8,
  output Q_9,
  output nQ_9,
  output Q_10,
  output nQ_10,
  output [3:0] OUT_2,
  output [3:0] out_47,
  output [3:0] out_48
);

  wire and_1_out, and_2_out, and_3_out, and_4_out, button_1_out, button_2_out, CLK_2_out, CLK_3_out,
       CLK_4_out, CLK_5_out, CLK_6_out, CLK_7_out, CLK_8_out, CLK_9_out, CLK_10_out, CLK_11_out, CLK_out,
       clock_1_out, clock_2_out, comparator_1_gt, nand_3_out, nand_4_out, nand_5_out, nand_6_out, nand_7_out,
       nand_8_out, nand_11_out, nand_12_out, nand_13_out, nand_14_out, nand_17_out, nand_18_out, nand_19_out,
       nand_20_out, not_1_out, not_2_out, not_3_out, not_4_out, not_5_out, not_6_out, not_7_out, not_8_out,
       not_9_out, not_10_out, or_1_out, or_2_out, or_3_out, or_4_out, or_5_out, \搭建_d_锁存器_1_q ;
  wire [3:0] adder_1_out, multiplexer_1_out, multiplexer_2_out, subtractor_1_out;

  Clock CLK (.out(CLK_out));
  Clock CLK_2 (.out(CLK_2_out));
  Clock CLK_3 (.out(CLK_3_out));
  Clock CLK_4 (.out(CLK_4_out));
  Clock CLK_5 (.out(CLK_5_out));
  Clock clock_1 (.out(clock_1_out));
  Button button_1 (.out(button_1_out));
  not not_1 (not_1_out, D_4);
  not not_2 (not_2_out, CLK_4_out);
  or or_1 (or_1_out, D_8, ST);
  Adder #(.width(4)) adder_1 (.a(out_48), .b(4'b0001), .out(adder_1_out), .cin(1'b0));  // open: cout
  nand nand_1 (Q, nS, nQ_3);
  nand nand_2 (nQ_3, Q, nR);
  nand nand_3 (nand_3_out, D_4, CLK_3_out);
  nand nand_4 (nand_4_out, not_1_out, CLK_3_out);
  nand nand_5 (nand_5_out, nand_8_out, CLK_out, nand_6_out);
  nand nand_6 (nand_6_out, nand_5_out, D_9, nRST_4);
  not not_3 (not_3_out, button_1_out);
  \搭建_D_锁存器  \u_搭建_d_锁存器_1  (.Q(\搭建_d_锁存器_1_q ), .CLK(not_2_out), .D(D_7));  // open: nQ
  \搭建_D_触发器  \u_搭建_d_触发器_1  (.D(or_1_out), .Q(Q_9), .nQ(nQ_9), .CLK(CLK_5_out));
  nand nand_7 (nand_7_out, nand_6_out, nand_8_out);
  nand nand_8 (nand_8_out, nand_7_out, CLK_out, nRST_4);
  \异步复位D触发器  \u_异步复位d触发器_1  (.Q(OUT_2[0]), .D(IN_2[0]), .nRST(nR_3), .CLK(CLK_2_out));  // open: nQ
  \异步复位D触发器  \u_异步复位d触发器_2  (.Q(OUT_2[1]), .D(IN_2[1]), .nRST(nR_3), .CLK(CLK_2_out));  // open: nQ
  \异步复位D触发器  \u_异步复位d触发器_3  (.Q(OUT_2[2]), .D(IN_2[2]), .nRST(nR_3), .CLK(CLK_2_out));  // open: nQ
  \异步复位D触发器  \u_异步复位d触发器_4  (.Q(OUT_2[3]), .D(IN_2[3]), .nRST(nR_3), .CLK(CLK_2_out));  // open: nQ
  \异步复位寄存器  \u_异步复位寄存器_1  (.OUT(out_48), .CLK(clock_1_out), .nR(not_3_out), .IN(adder_1_out));
  \搭建_SR_锁存器  \u_搭建_sr_锁存器_1  (.nS(nand_3_out), .nR(nand_4_out), .Q(Q_5), .nQ(nQ_5));
  \搭建_SR_锁存器  \u_搭建_sr_锁存器_2  ();  // open: nS, nR, Q, nQ
  \搭建_D_锁存器  \u_搭建_d_锁存器_2  (.Q(Q_8), .nQ(nQ_8), .CLK(CLK_4_out), .D(\搭建_d_锁存器_1_q ));
  nand nand_9 (Q_10, nand_8_out, nQ_10);
  nand nand_10 (nQ_10, Q_10, nand_5_out, nRST_4);
  Hex_Digit_Display hex_digit_display_1 (.value(out_48), .dp(1'b0));
  \同步置位D触发器  \u_同步置位d触发器_1  ();  // open: CLK, D, ST, Q, nQ
  \搭建_D_锁存器  \u_搭建_d_锁存器_3  ();  // open: Q, nQ, CLK, D
  \搭建_D_触发器  \u_搭建_d_触发器_2  ();  // open: D, Q, nQ, CLK
  Clock CLK_6 (.out(CLK_6_out));
  Clock CLK_7 (.out(CLK_7_out));
  not not_4 (not_4_out, RST);
  \异步复位D触发器  \u_异步复位d触发器_5  ();  // open: Q, nQ, D, nRST, CLK
  \异步复位寄存器  \u_异步复位寄存器_2  ();  // open: OUT, CLK, nR, IN
  and and_1 (and_1_out, D, nRST);
  and and_2 (and_2_out, D_5, not_4_out);
  \搭建_D_触发器  \u_搭建_d_触发器_3  (.D(and_1_out), .Q(Q_2), .nQ(nQ), .CLK(CLK_6_out));
  \搭建_D_触发器  \u_搭建_d_触发器_4  (.D(and_2_out), .Q(Q_6), .nQ(nQ_6), .CLK(CLK_7_out));
  Clock CLK_8 (.out(CLK_8_out));
  Clock CLK_9 (.out(CLK_9_out));
  Clock clock_2 (.out(clock_2_out));
  Button button_2 (.out(button_2_out));
  and and_3 (and_3_out, D_2, nRST_2);
  and and_4 (and_4_out, D_6, not_5_out);
  not not_5 (not_5_out, RST_2);
  Subtractor #(.width(4)) subtractor_1 (.a(out_47), .b(4'b0001), .out(subtractor_1_out), .bin(1'b0));  // open: bout
  not not_6 (not_6_out, button_2_out);
  Comparator #(.width(4), .mode("unsigned")) comparator_1 (
    .a(4'b1001), .b(subtractor_1_out), .gt(comparator_1_gt));  // open: eq, lt
  \搭建_D_触发器  \u_搭建_d_触发器_5  (.D(and_3_out), .Q(Q_3), .nQ(nQ_2), .CLK(CLK_8_out));
  \搭建_D_触发器  \u_搭建_d_触发器_6  (.D(and_4_out), .Q(Q_7), .nQ(nQ_7), .CLK(CLK_9_out));
  Multiplexer #(.width(4)) multiplexer_1 (
    .in0(4'b1001), .in1(subtractor_1_out), .out(multiplexer_1_out), .sel(comparator_1_gt), .en(1'b1));
  Clock CLK_10 (.out(CLK_10_out));
  \异步定复位寄存器  \u_异步定复位寄存器_1  (
    .IN(multiplexer_1_out), .CLK(clock_2_out), .nR(not_6_out), .Reset_Value(4'b1001), .OUT(out_47));
  Hex_Digit_Display hex_digit_display_2 (.value(out_47), .dp(1'b0));
  nand nand_11 (nand_11_out, nST, nand_14_out, nand_12_out);
  nand nand_12 (nand_12_out, nand_11_out, CLK_10_out, nRST_3);
  nand nand_13 (nand_13_out, nand_12_out, CLK_10_out, nand_14_out);
  nand nand_14 (nand_14_out, nand_13_out, D_3, nRST_3);
  Clock CLK_11 (.out(CLK_11_out));
  Multiplexer #(.width(4)) multiplexer_2 (
    .in0(Reset_Value), .in1(4'b1111), .out(multiplexer_2_out), .sel(nR_2), .en(1'b1));
  nand nand_15 (Q_4, nST, nand_12_out, nQ_4);
  nand nand_16 (nQ_4, Q_4, nand_13_out, nRST_3);
  not not_7 (not_7_out, nR_2);
  not not_8 (not_8_out, nR_2);
  not not_9 (not_9_out, nR_2);
  not not_10 (not_10_out, nR_2);
  nand nand_17 (nand_17_out, not_7_out, multiplexer_2_out[0]);
  or or_2 (or_2_out, nR_2, multiplexer_2_out[0]);
  nand nand_18 (nand_18_out, not_8_out, multiplexer_2_out[1]);
  or or_3 (or_3_out, nR_2, multiplexer_2_out[1]);
  nand nand_19 (nand_19_out, not_9_out, multiplexer_2_out[2]);
  or or_4 (or_4_out, nR_2, multiplexer_2_out[2]);
  nand nand_20 (nand_20_out, not_10_out, multiplexer_2_out[3]);
  or or_5 (or_5_out, nR_2, multiplexer_2_out[3]);
  \异步复置位D触发器  \u_异步复置位d触发器_1  (
    .nST(nand_17_out), .Q(OUT[0]), .CLK(CLK_11_out), .D(IN[0]), .nRST(or_2_out));  // open: nQ
  \异步复置位D触发器  \u_异步复置位d触发器_2  (
    .nST(nand_18_out), .Q(OUT[1]), .CLK(CLK_11_out), .D(IN[1]), .nRST(or_3_out));  // open: nQ
  \异步复置位D触发器  \u_异步复置位d触发器_3  (
    .nST(nand_19_out), .Q(OUT[2]), .CLK(CLK_11_out), .D(IN[2]), .nRST(or_4_out));  // open: nQ
  \异步复置位D触发器  \u_异步复置位d触发器_4  (
    .nST(nand_20_out), .Q(OUT[3]), .CLK(CLK_11_out), .D(IN[3]), .nRST(or_5_out));  // open: nQ
  \异步复置位D触发器  \u_异步复置位d触发器_5  ();  // open: nST, Q, CLK, nQ, D, nRST
  \异步定复位寄存器  \u_异步定复位寄存器_2  ();  // open: IN, CLK, nR, Reset_Value, OUT

  // Notes on the sheet:
  //   D1
  //   D2
  //   OUEDRAOGO EZEKIEL B.
  //   PL19215001
  //   OUEDRAOGO EZEKIEL B.
  //   PL19215001
  //   OUEDRAOGO EZEKIEL B.
  //   PL19215001
  //   PL19215001
  //   OUEDRAOGO EZEKIEL B.
  //   PL19215001
  //   OUEDRAOGO EZEKIEL B.
  //   PL19215001
  //   OUEDRAOGO EZEKIEL B.
  //   PL19215001
  //   OUEDRAOGO EZEKIEL B.
  //   复位（低电平有效）D触发器
  //   复位（高电平有效）D触发器
  //   OUEDRAOGO EZEKIEL B.
  //   PL19215001
  //   OUEDRAOGO EZEKIEL B.
  //   PL19215001
  //   PL19215001
  //   OUEDRAOGO EZEKIEL B.
  //   PL19215001
  //   FF0
  //   FF1
  //   FF2
  //   FF3
  //   OUEDRAOGO EZEKIEL B.
  //   PL19215001
  //   OUEDRAOGO EZEKIEL B.
endmodule

module \搭建双稳态电路  (
  input  in_1,
  input  in_2,
  output out_3,
  output out_4,
  output out_5,
  output out_6
);

  not not_1 (out_3, out_5);
  not not_2 (out_5, out_3);
  not not_3 (out_4, out_6);
  not not_4 (out_6, out_4);
endmodule

// SR_lATCH
module \搭建_SR_锁存器  (
  input  nS,
  input  nR,
  output Q,
  output nQ
);

  nand nand_1 (Q, nS, nQ);
  nand nand_2 (nQ, Q, nR);

  // Notes on the sheet:
  //   PL19215001
  //   OUEDRAOGO EZEKIEL B.
endmodule

// D_LATCH
module \搭建_D_锁存器  (
  input  CLK,
  input  D,
  output Q,
  output nQ
);

  wire nand_1_out, nand_2_out, not_1_out;

  nand nand_1 (nand_1_out, D, CLK);
  not not_1 (not_1_out, D);
  nand nand_2 (nand_2_out, not_1_out, CLK);
  \搭建_SR_锁存器  \u_搭建_sr_锁存器_1  (.nS(nand_1_out), .nR(nand_2_out), .Q(Q), .nQ(nQ));
endmodule

// D_FF
module \搭建_D_触发器  (
  input  CLK,
  input  D,
  output Q,
  output nQ
);

  wire not_1_out, \搭建_d_锁存器_1_q ;

  not not_1 (not_1_out, CLK);
  \搭建_D_锁存器  \u_搭建_d_锁存器_1  (.Q(\搭建_d_锁存器_1_q ), .CLK(not_1_out), .D(D));  // open: nQ
  \搭建_D_锁存器  \u_搭建_d_锁存器_2  (.Q(Q), .nQ(nQ), .CLK(CLK), .D(\搭建_d_锁存器_1_q ));

  // Notes on the sheet:
  //   D1
  //   D2
endmodule

// D_FF_R
module \同步复位D触发器  (
  input  CLK,
  input  D,
  input  RST,
  output Q,
  output nQ
);

  wire and_1_out, not_1_out;

  Clock clock_1 (.out(CLK));
  not not_1 (not_1_out, RST);
  and and_1 (and_1_out, D, not_1_out);
  \搭建_D_触发器  \u_搭建_d_触发器_1  (.D(and_1_out), .Q(Q), .nQ(nQ), .CLK(CLK));
endmodule

// D_FF_S
module \同步置位D触发器  (
  input  CLK,
  input  D,
  input  ST,
  output Q,
  output nQ
);

  wire or_1_out;

  or or_1 (or_1_out, D, ST);
  \搭建_D_触发器  \u_搭建_d_触发器_1  (.D(or_1_out), .Q(Q), .nQ(nQ), .CLK(CLK));

  // Notes on the sheet:
  //   PL19215001
  //   OUEDRAOGO EZEKIEL B.
endmodule

// D_FF_R_S
module \同步复置位D出发器  (
  input  CLK,
  input  ST,
  input  D,
  input  RST,
  output Q,
  output nQ
);

  wire and_1_out, not_1_out, or_1_out;

  Clock clock_1 (.out(CLK));
  not not_1 (not_1_out, RST);
  and and_1 (and_1_out, D, not_1_out);
  or or_1 (or_1_out, ST, and_1_out);
  \搭建_D_触发器  \u_搭建_d_触发器_1  (.D(or_1_out), .Q(Q), .nQ(nQ), .CLK(CLK));

  // Notes on the sheet:
  //   PL19215001
  //   OUEDRAOGO EZEKIEL B.
endmodule

// D_FF_R_A
module \异步复位D触发器  (
  input  CLK,
  input  D,
  input  nRST,
  output Q,
  output nQ
);

  wire nand_1_out, nand_2_out, nand_3_out, nand_4_out;

  nand nand_1 (nand_1_out, nand_4_out, nand_2_out);
  nand nand_2 (nand_2_out, nand_1_out, CLK, nRST);
  nand nand_3 (nand_3_out, nand_2_out, CLK, nand_4_out);
  nand nand_4 (nand_4_out, nand_3_out, D, nRST);
  nand nand_5 (Q, nand_2_out, nQ);
  nand nand_6 (nQ, Q, nand_3_out, nRST);

  // Notes on the sheet:
  //   PL19215001
  //   OUEDRAOGO EZEKIEL B.
endmodule

module \异步置位D触发器  (
  input  nST,
  input  CLK,
  input  D,
  output Q,
  output nQ
);

  wire nand_1_out, nand_2_out, nand_3_out, nand_4_out;

  Clock u_CLK (.out(CLK));
  nand nand_1 (nand_1_out, nST, nand_4_out, nand_2_out);
  nand nand_2 (nand_2_out, nand_1_out, CLK);
  nand nand_3 (nand_3_out, nand_2_out, CLK, nand_4_out);
  nand nand_4 (nand_4_out, nand_3_out, D);
  nand nand_5 (Q, nST, nand_2_out, nQ);
  nand nand_6 (nQ, Q, nand_3_out);

  // Notes on the sheet:
  //   PL19215001
  //   OUEDRAOGO EZEKIEL B.
endmodule

// D_FF_S_R_A
module \异步复置位D触发器  (
  input  nST,
  input  CLK,
  input  D,
  input  nRST,
  output Q,
  output nQ
);

  wire nand_1_out, nand_2_out, nand_3_out, nand_4_out;

  Clock clock_1 (.out(CLK));
  nand nand_1 (nand_1_out, nST, nand_4_out, nand_2_out);
  nand nand_2 (nand_2_out, nand_1_out, CLK, nRST);
  nand nand_3 (nand_3_out, nand_2_out, CLK, nand_4_out);
  nand nand_4 (nand_4_out, nand_3_out, D, nRST);
  nand nand_5 (Q, nST, nand_2_out, nQ);
  nand nand_6 (nQ, Q, nand_3_out, nRST);

  // Notes on the sheet:
  //   PL19215001
  //   OUEDRAOGO EZEKIEL B.
endmodule

// REG_R
module \同步复位寄存器  (
  input  [3:0] IN,
  input  CLK,
  input  R,
  output [3:0] OUT
);

  Clock clock_1 (.out(CLK));
  \同步复位D触发器  \u_同步复位d触发器_1  (.D(IN[0]), .RST(R), .Q(OUT[0]), .CLK(CLK));  // open: nQ
  \同步复位D触发器  \u_同步复位d触发器_2  (.D(IN[1]), .RST(R), .Q(OUT[1]), .CLK(CLK));  // open: nQ
  \同步复位D触发器  \u_同步复位d触发器_3  (.D(IN[2]), .RST(R), .Q(OUT[2]), .CLK(CLK));  // open: nQ
  \同步复位D触发器  \u_同步复位d触发器_4  (.D(IN[3]), .RST(R), .Q(OUT[3]), .CLK(CLK));  // open: nQ
endmodule

// REG_R_A
module \异步复位寄存器  (
  input  [3:0] IN,
  input  CLK,
  input  nR,
  output [3:0] OUT
);

  \异步复位D触发器  \u_异步复位d触发器_1  (.Q(OUT[0]), .D(IN[0]), .nRST(nR), .CLK(CLK));  // open: nQ
  \异步复位D触发器  \u_异步复位d触发器_2  (.Q(OUT[1]), .D(IN[1]), .nRST(nR), .CLK(CLK));  // open: nQ
  \异步复位D触发器  \u_异步复位d触发器_3  (.Q(OUT[2]), .D(IN[2]), .nRST(nR), .CLK(CLK));  // open: nQ
  \异步复位D触发器  \u_异步复位d触发器_4  (.Q(OUT[3]), .D(IN[3]), .nRST(nR), .CLK(CLK));  // open: nQ

  // Notes on the sheet:
  //   OUEDRAOGO EZEKIEL B.
  //   PL19215001
endmodule

module \异步定复位寄存器  (
  input  [3:0] IN,
  input  CLK,
  input  [3:0] Reset_Value,
  input  nR,
  output [3:0] OUT
);

  wire nand_1_out, nand_2_out, nand_3_out, nand_4_out, not_1_out, not_2_out, not_3_out, not_4_out, or_1_out,
       or_2_out, or_3_out, or_4_out;
  wire [3:0] multiplexer_1_out;

  Clock clock_1 (.out(CLK));
  Multiplexer #(.width(4)) multiplexer_1 (
    .in0(Reset_Value), .in1(4'b1111), .out(multiplexer_1_out), .sel(nR), .en(1'b1));
  not not_1 (not_1_out, nR);
  not not_2 (not_2_out, nR);
  not not_3 (not_3_out, nR);
  not not_4 (not_4_out, nR);
  nand nand_1 (nand_1_out, not_1_out, multiplexer_1_out[0]);
  or or_1 (or_1_out, nR, multiplexer_1_out[0]);
  nand nand_2 (nand_2_out, not_2_out, multiplexer_1_out[1]);
  or or_2 (or_2_out, nR, multiplexer_1_out[1]);
  nand nand_3 (nand_3_out, not_3_out, multiplexer_1_out[2]);
  or or_3 (or_3_out, nR, multiplexer_1_out[2]);
  nand nand_4 (nand_4_out, not_4_out, multiplexer_1_out[3]);
  or or_4 (or_4_out, nR, multiplexer_1_out[3]);
  \异步复置位D触发器  \u_异步复置位d触发器_1  (.nST(nand_1_out), .Q(OUT[0]), .CLK(CLK), .D(IN[0]), .nRST(or_1_out));  // open: nQ
  \异步复置位D触发器  \u_异步复置位d触发器_2  (.nST(nand_2_out), .Q(OUT[1]), .CLK(CLK), .D(IN[1]), .nRST(or_2_out));  // open: nQ
  \异步复置位D触发器  \u_异步复置位d触发器_3  (.nST(nand_3_out), .Q(OUT[2]), .CLK(CLK), .D(IN[2]), .nRST(or_3_out));  // open: nQ
  \异步复置位D触发器  \u_异步复置位d触发器_4  (.nST(nand_4_out), .Q(OUT[3]), .CLK(CLK), .D(IN[3]), .nRST(or_4_out));  // open: nQ

  // Notes on the sheet:
  //   FF0
  //   FF1
  //   FF2
  //   FF3
endmodule

module \计数0_15  (
  output [3:0] out_1
);

  wire button_1_out, clock_1_out, not_1_out;
  wire [3:0] adder_1_out;

  Adder #(.width(4)) adder_1 (.a(out_1), .b(4'b0001), .out(adder_1_out), .cin(1'b0));  // open: cout
  Clock clock_1 (.out(clock_1_out));
  Button button_1 (.out(button_1_out));
  not not_1 (not_1_out, button_1_out);
  \异步复位寄存器  \u_异步复位寄存器_1  (.OUT(out_1), .CLK(clock_1_out), .nR(not_1_out), .IN(adder_1_out));
  Hex_Digit_Display hex_digit_display_1 (.value(out_1), .dp(1'b0));

  // Notes on the sheet:
  //   PL19215001
  //   OUEDRAOGO EZEKIEL B.
endmodule

module \计数9_0  (
  output [3:0] out_1
);

  wire button_1_out, clock_1_out, comparator_1_gt, not_1_out;
  wire [3:0] multiplexer_1_out, subtractor_1_out;

  Clock clock_1 (.out(clock_1_out));
  Button button_1 (.out(button_1_out));
  Subtractor #(.width(4)) subtractor_1 (.a(out_1), .b(4'b0001), .out(subtractor_1_out), .bin(1'b0));  // open: bout
  not not_1 (not_1_out, button_1_out);
  Comparator #(.width(4), .mode("unsigned")) comparator_1 (
    .a(4'b1001), .b(subtractor_1_out), .gt(comparator_1_gt));  // open: eq, lt
  Multiplexer #(.width(4)) multiplexer_1 (
    .in0(4'b1001), .in1(subtractor_1_out), .out(multiplexer_1_out), .sel(comparator_1_gt), .en(1'b1));
  \异步定复位寄存器  \u_异步定复位寄存器_1  (
    .IN(multiplexer_1_out), .CLK(clock_1_out), .nR(not_1_out), .Reset_Value(4'b1001), .OUT(out_1));
  Hex_Digit_Display hex_digit_display_1 (.value(out_1), .dp(1'b0));

  // Notes on the sheet:
  //   PL19215001
  //   OUEDRAOGO EZEKIEL B.
endmodule
