// Logisim project 实验06_FPGA原理及Vivado综合.circ as structural Verilog: 7 circuits, main circuit main
module main (
  input  in1,
  input  in2,
  input  in3,
  input  [1:0] in_4,
  input  [1:0] in_5,
  input  [1:0] in_6,
  output out1,
  output out1_2,
  output out1_3
);

  wire decoder_1_out1, decoder_1_out2, decoder_1_out3, decoder_2_out1, decoder_2_out2, decoder_2_out3,
       decoder_3_out1, decoder_3_out2, decoder_3_out3;

  Decoder #(.select(2)) decoder_1 (
    .out1(decoder_1_out1), .out2(decoder_1_out2), .out3(decoder_1_out3), .sel(in_4));  // open: out0, en
  assign out1 = decoder_1_out1 ? in1 : 1'bz;  // Controlled_Buffer controlled_buffer_1
  assign out1 = decoder_1_out2 ? in2 : 1'bz;  // Controlled_Buffer controlled_buffer_2
  assign out1 = decoder_1_out3 ? in3 : 1'bz;  // Controlled_Buffer controlled_buffer_3
  Decoder #(.select(2)) decoder_2 (
    .out1(decoder_2_out1), .out2(decoder_2_out2), .out3(decoder_2_out3), .sel(in_5));  // open: out0, en
  assign out1_2 = decoder_2_out1 ? in1 : 1'bz;  // Controlled_Buffer controlled_buffer_4
  assign out1_2 = decoder_2_out2 ? in2 : 1'bz;  // Controlled_Buffer controlled_buffer_5
  assign out1_2 = decoder_2_out3 ? in3 : 1'bz;  // Controlled_Buffer controlled_buffer_6
  Decoder #(.select(2)) decoder_3 (
    .out1(decoder_3_out1), .out2(decoder_3_out2), .out3(decoder_3_out3), .sel(in_6));  // open: out0, en
  assign out1_3 = decoder_3_out1 ? in1 : 1'bz;  // Controlled_Buffer controlled_buffer_7
  assign out1_3 = decoder_3_out2 ? in2 : 1'bz;  // Controlled_Buffer controlled_buffer_8
  assign out1_3 = decoder_3_out3 ? in3 : 1'bz;  // Controlled_Buffer controlled_buffer_9
endmodule

module x01 (
  input  in_1,
  input  in_2,
  output out_3
);

  RAM #(.addrWidth(2), .dataWidth(1)) ram_1 (.addr({in_2, in_1}), .data(out_3));  // open: sel, clk, ld, clr
endmodule

module x02 (
  input  in_1,
  input  in_2,
  output out_3
);

  wire clock_1_out, d_ff_1_q, ram_1_data;

  Clock clock_1 (.out(clock_1_out));
  RAM #(.addrWidth(2), .dataWidth(1)) ram_1 (.addr({in_2, in_1}), .data(ram_1_data));  // open: sel, clk, ld, clr
  D_Flip_Flop d_ff_1 (.clk(clock_1_out), .D(ram_1_data), .Q(d_ff_1_q));  // open: Qn, preset, en, reset
  Multiplexer multiplexer_1 (.in0(d_ff_1_q), .in1(ram_1_data), .out(out_3), .sel(1'b1));  // open: en
endmodule

module x03 (
  input  in1,
  input  in2,
  input  in3,
  input  [1:0] in_4,
  input  [1:0] in_5,
  input  [1:0] in_6,
  output out1,
  output out1_2,
  output out1_3
);

  wire decoder_1_out1, decoder_1_out2, decoder_1_out3, decoder_2_out1, decoder_2_out2, decoder_2_out3,
       decoder_3_out1, decoder_3_out2, decoder_3_out3;

  Decoder #(.select(2)) decoder_1 (
    .out1(decoder_1_out1), .out2(decoder_1_out2), .out3(decoder_1_out3), .sel(in_4));  // open: out0, en
  assign out1 = decoder_1_out1 ? in1 : 1'bz;  // Controlled_Buffer controlled_buffer_1
  assign out1 = decoder_1_out2 ? in2 : 1'bz;  // Controlled_Buffer controlled_buffer_2
  assign out1 = decoder_1_out3 ? in3 : 1'bz;  // Controlled_Buffer controlled_buffer_3
  Decoder #(.select(2)) decoder_2 (
    .out1(decoder_2_out1), .out2(decoder_2_out2), .out3(decoder_2_out3), .sel(in_5));  // open: out0, en
  assign out1_2 = decoder_2_out1 ? in1 : 1'bz;  // Controlled_Buffer controlled_buffer_4
  assign out1_2 = decoder_2_out2 ? in2 : 1'bz;  // Controlled_Buffer controlled_buffer_5
  assign out1_2 = decoder_2_out3 ? in3 : 1'bz;  // Controlled_Buffer controlled_buffer_6
  Decoder #(.select(2)) decoder_3 (
    .out1(decoder_3_out1), .out2(decoder_3_out2), .out3(decoder_3_out3), .sel(in_6));  // open: out0, en
  assign out1_3 = decoder_3_out1 ? in1 : 1'bz;  // Controlled_Buffer controlled_buffer_7
  assign out1_3 = decoder_3_out2 ? in2 : 1'bz;  // Controlled_Buffer controlled_buffer_8
  assign out1_3 = decoder_3_out3 ? in3 : 1'bz;  // Controlled_Buffer controlled_buffer_9
endmodule

module x04 (
  input  in1,
  input  in2,
  input  a,
  input  b,
  output out1,
  output out1_2,
  output out1_3
);

  wire clk_out, d_ff_1_q, decoder_1_out1, decoder_1_out2, decoder_1_out3, decoder_2_out1, decoder_2_out2,
       decoder_2_out3, decoder_3_out1, decoder_3_out2, decoder_3_out3, multiplexer_2_out, ram_1_data;
  wire [0:0] multiplexer_1_out;

  Clock clk (.out(clk_out));
  Multiplexer multiplexer_1 (.in0(out1), .in1(a), .out(multiplexer_1_out[0]), .sel(1'b1));  // open: en
  RAM #(.addrWidth(2), .dataWidth(1)) ram_1 (
    .addr({b, multiplexer_1_out[0]}), .data(ram_1_data));  // open: sel, clk, ld, clr
  D_Flip_Flop d_ff_1 (.clk(clk_out), .D(ram_1_data), .Q(d_ff_1_q));  // open: Qn, preset, en, reset
  Multiplexer multiplexer_2 (.in0(d_ff_1_q), .in1(ram_1_data), .out(multiplexer_2_out), .sel(1'b1));  // open: en
  assign out1 = decoder_1_out1 ? in1 : 1'bz;  // Controlled_Buffer controlled_buffer_1
  assign out1 = decoder_1_out2 ? in2 : 1'bz;  // Controlled_Buffer controlled_buffer_2
  assign out1 = decoder_1_out3 ? multiplexer_2_out : 1'bz;  // Controlled_Buffer controlled_buffer_3
  Decoder #(.select(2)) decoder_1 (
    .out1(decoder_1_out1), .out2(decoder_1_out2), .out3(decoder_1_out3), .sel(2'b11));  // open: out0, en
  Decoder #(.select(2)) decoder_2 (
    .out1(decoder_2_out1), .out2(decoder_2_out2), .out3(decoder_2_out3), .sel(2'b11));  // open: out0, en
  assign out1_2 = decoder_2_out1 ? in1 : 1'bz;  // Controlled_Buffer controlled_buffer_4
  assign out1_2 = decoder_2_out2 ? in2 : 1'bz;  // Controlled_Buffer controlled_buffer_5
  assign out1_2 = decoder_2_out3 ? multiplexer_2_out : 1'bz;  // Controlled_Buffer controlled_buffer_6
  assign out1_3 = decoder_3_out1 ? in1 : 1'bz;  // Controlled_Buffer controlled_buffer_7
  assign out1_3 = decoder_3_out2 ? in2 : 1'bz;  // Controlled_Buffer controlled_buffer_8
  assign out1_3 = decoder_3_out3 ? multiplexer_2_out : 1'bz;  // Controlled_Buffer controlled_buffer_9
  Decoder #(.select(2)) decoder_3 (
    .out1(decoder_3_out1), .out2(decoder_3_out2), .out3(decoder_3_out3), .sel(2'b11));  // open: out0, en
endmodule

module x05 (
  input  in1,
  input  in2,
  input  a,
  input  b,
  output out1,
  output out1_2,
  output out1_3,
  output out_8,
  output out_9
);

  wire buffer_1_out, buffer_2_out, clk_out, d_ff_1_q, decoder_1_out1, decoder_1_out2, decoder_1_out3,
       decoder_2_out1, decoder_2_out2, decoder_2_out3, decoder_3_out1, decoder_3_out2, decoder_3_out3,
       multiplexer_2_out, multiplexer_3_out;
  wire [0:0] multiplexer_1_out;

  Clock clk (.out(clk_out));
  Multiplexer multiplexer_1 (.in0(out1), .in1(a), .out(multiplexer_1_out[0]), .sel(1'b1));  // open: en
  Multiplexer #(.select(2)) multiplexer_2 (
    .in0(1'b1), .in1(1'b1), .in2(1'b1), .in3(1'b0), .out(multiplexer_2_out), .sel({b, multiplexer_1_out[0]}));  // open: en
  D_Flip_Flop d_ff_1 (.clk(clk_out), .D(multiplexer_2_out), .Q(d_ff_1_q));  // open: Qn, preset, en, reset
  Multiplexer multiplexer_3 (.in0(d_ff_1_q), .in1(multiplexer_2_out), .out(multiplexer_3_out), .sel(1'b1));  // open: en
  Decoder #(.select(2)) decoder_1 (
    .out1(decoder_1_out1), .out2(decoder_1_out2), .out3(decoder_1_out3), .sel(2'b11));  // open: out0, en
  assign out1 = decoder_1_out1 ? in1 : 1'bz;  // Controlled_Buffer controlled_buffer_1
  assign out1 = decoder_1_out2 ? in2 : 1'bz;  // Controlled_Buffer controlled_buffer_2
  assign out1 = decoder_1_out3 ? multiplexer_3_out : 1'bz;  // Controlled_Buffer controlled_buffer_3
  assign out1_2 = decoder_2_out1 ? in1 : 1'bz;  // Controlled_Buffer controlled_buffer_4
  assign out1_2 = decoder_2_out2 ? in2 : 1'bz;  // Controlled_Buffer controlled_buffer_5
  assign out1_2 = decoder_2_out3 ? multiplexer_3_out : 1'bz;  // Controlled_Buffer controlled_buffer_6
  Decoder #(.select(2)) decoder_2 (
    .out1(decoder_2_out1), .out2(decoder_2_out2), .out3(decoder_2_out3), .sel(2'b01));  // open: out0, en
  Decoder #(.select(2)) decoder_3 (
    .out1(decoder_3_out1), .out2(decoder_3_out2), .out3(decoder_3_out3), .sel(2'b10));  // open: out0, en
  assign out1_3 = decoder_3_out1 ? in1 : 1'bz;  // Controlled_Buffer controlled_buffer_7
  assign out1_3 = decoder_3_out2 ? in2 : 1'bz;  // Controlled_Buffer controlled_buffer_8
  assign out1_3 = decoder_3_out3 ? multiplexer_3_out : 1'bz;  // Controlled_Buffer controlled_buffer_9
  buf buffer_1 (buffer_1_out, out_8);
  assign out_8 = 1'b1 ? out1_2 : 1'bz;  // Controlled_Buffer controlled_buffer_10
  buf buffer_2 (buffer_2_out, out_9);
  assign out_9 = 1'b1 ? out1_3 : 1'bz;  // Controlled_Buffer controlled_buffer_11
endmodule

module _051 (
  input  in1,
  input  in2,
  input  a,
  input  b,
  output out1,
  output out1_2,
  output out1_3,
  output out_8,
  output out_9
);

  wire buffer_1_out, buffer_2_out, clk_out, d_ff_1_q, decoder_1_out1, decoder_1_out2, decoder_1_out3,
       decoder_2_out1, decoder_2_out2, decoder_2_out3, decoder_3_out1, decoder_3_out2, decoder_3_out3,
       multiplexer_2_out, multiplexer_3_out;
  wire [0:0] multiplexer_1_out;

  Clock clk (.out(clk_out));
  Multiplexer multiplexer_1 (.in0(out1), .in1(a), .out(multiplexer_1_out[0]), .sel(1'b0));  // open: en
  Multiplexer #(.select(2)) multiplexer_2 (
    .in0(1'b1), .in1(1'b0), .in2(1'b1), .in3(1'b0), .out(multiplexer_2_out), .sel({b, multiplexer_1_out[0]}));  // open: en
  D_Flip_Flop d_ff_1 (.clk(clk_out), .D(multiplexer_2_out), .Q(d_ff_1_q));  // open: Qn, preset, en, reset
  Multiplexer multiplexer_3 (.in0(d_ff_1_q), .in1(multiplexer_2_out), .out(multiplexer_3_out), .sel(1'b0));  // open: en
  Decoder #(.select(2)) decoder_1 (
    .out1(decoder_1_out1), .out2(decoder_1_out2), .out3(decoder_1_out3), .sel(2'b11));  // open: out0, en
  assign out1 = decoder_1_out1 ? in1 : 1'bz;  // Controlled_Buffer controlled_buffer_1
  assign out1 = decoder_1_out2 ? in2 : 1'bz;  // Controlled_Buffer controlled_buffer_2
  assign out1 = decoder_1_out3 ? multiplexer_3_out : 1'bz;  // Controlled_Buffer controlled_buffer_3
  assign out1_2 = decoder_2_out1 ? in1 : 1'bz;  // Controlled_Buffer controlled_buffer_4
  assign out1_2 = decoder_2_out2 ? in2 : 1'bz;  // Controlled_Buffer controlled_buffer_5
  assign out1_2 = decoder_2_out3 ? multiplexer_3_out : 1'bz;  // Controlled_Buffer controlled_buffer_6
  Decoder #(.select(2)) decoder_2 (
    .out1(decoder_2_out1), .out2(decoder_2_out2), .out3(decoder_2_out3), .sel(2'b01));  // open: out0, en
  Decoder #(.select(2)) decoder_3 (
    .out1(decoder_3_out1), .out2(decoder_3_out2), .out3(decoder_3_out3), .sel(2'b11));  // open: out0, en
  assign out1_3 = decoder_3_out1 ? in1 : 1'bz;  // Controlled_Buffer controlled_buffer_7
  assign out1_3 = decoder_3_out2 ? in2 : 1'bz;  // Controlled_Buffer controlled_buffer_8
  assign out1_3 = decoder_3_out3 ? multiplexer_3_out : 1'bz;  // Controlled_Buffer controlled_buffer_9
  buf buffer_1 (buffer_1_out, out_8);
  assign out_8 = 1'b1 ? out1_2 : 1'bz;  // Controlled_Buffer controlled_buffer_10
  buf buffer_2 (buffer_2_out, out_9);
  assign out_9 = 1'b1 ? out1_3 : 1'bz;  // Controlled_Buffer controlled_buffer_11
endmodule
