// Logisim project 实验07_FPGA实验平台及IP核使用.circ as structural Verilog: 2 circuits, main circuit main
module main (
  input  [3:0] in_1
);

  wire [7:0] rom_1_data;

  ROM #(.addrWidth(4)) rom_1 (.addr(in_1), .data(rom_1_data));  // open: sel
  Hex_Digit_Display hex_digit_display_1 (.value(rom_1_data[3:0]));  // open: dp

  // Notes on the sheet:
  //   contents of rom_1 (hex, n*v repeats v):
  //   0 1 2 3 4 5 6 7 8 9 a b c d e f
endmodule

module RAM (
  input  [15:0] in_1,
  input  [1:0] in_2,
  input  in_3,
  input  in_4,
  input  in_5,
  input  in_6,
  output [15:0] out_7
);

  wire clock_1_out, not_1_out;
  wire [15:0] ram_1_data;

  Clock clock_1 (.out(clock_1_out));
  RAM_part #(.addrWidth(2), .dataWidth(16)) ram_1 (
    .addr(in_2), .data(ram_1_data), .sel(in_3), .clk(clock_1_out), .ld(in_4), .clr(in_6));
  assign ram_1_data = not_1_out ? in_1 : 16'bz;  // Controlled_Buffer controlled_buffer_1
  assign out_7 = in_5 ? ram_1_data : 16'bz;  // Controlled_Buffer controlled_buffer_2
  not not_1 (not_1_out, in_5);
endmodule
