// Logisim project 实验08_信号处理及有限状态机.circ as structural Verilog: 3 circuits, main circuit main
module main (
  input  in_1,
  output [1:0] curr,
  output [1:0] next
);

  wire clock_1_out, comparator_1_eq;

  Multiplexer #(.select(2), .width(2)) multiplexer_1 (
    .in0(2'b01), .in1(2'b10), .in2(2'b11), .in3(2'b00), .out(next), .sel(curr));  // open: en
  Clock clock_1 (.out(clock_1_out));
  D_Flip_Flop d_ff_1 (.clk(clock_1_out), .D(next[0]), .Q(curr[0]), .reset(in_1));  // open: Qn, preset, en
  D_Flip_Flop d_ff_2 (.clk(clock_1_out), .D(next[1]), .Q(curr[1]), .reset(in_1));  // open: Qn, preset, en
  LED led_1 (.in(comparator_1_eq));
  Comparator #(.width(2)) comparator_1 (.a(curr), .b(2'b11), .eq(comparator_1_eq));  // open: gt, lt
endmodule

module _081 (
  input  in_1,
  output [1:0] curr,
  output [1:0] next
);

  wire clock_1_out, comparator_1_eq;

  Multiplexer #(.select(2), .width(2)) multiplexer_1 (
    .in0(2'b01), .in1(2'b10), .in2(2'b11), .in3(2'b00), .out(next), .sel(curr));  // open: en
  Clock clock_1 (.out(clock_1_out));
  D_Flip_Flop d_ff_1 (.clk(clock_1_out), .D(next[0]), .Q(curr[0]), .reset(in_1));  // open: Qn, preset, en
  D_Flip_Flop d_ff_2 (.clk(clock_1_out), .D(next[1]), .Q(curr[1]), .reset(in_1));  // open: Qn, preset, en
  Comparator #(.width(2)) comparator_1 (.a(curr), .b(2'b11), .eq(comparator_1_eq));  // open: gt, lt
  LED led_1 (.in(comparator_1_eq));
endmodule

module _082 (
  input  sw,
  input  rst
);

  wire clk_out, d_ff_1_q, d_ff_2_q, xor_1_out;
  wire [3:0] counter_1_q;

  Clock clk (.out(clk_out));
  D_Flip_Flop d_ff_1 (.clk(clk_out), .D(sw), .Q(d_ff_1_q));  // open: Qn, preset, en, reset
  D_Flip_Flop d_ff_2 (.clk(clk_out), .D(d_ff_1_q), .Q(d_ff_2_q));  // open: Qn, preset, en, reset
  xor xor_1 (xor_1_out, d_ff_2_q, d_ff_1_q);
  Counter #(.width(4), .max('hf)) counter_1 (
    .count(xor_1_out), .Q(counter_1_q), .clk(clk_out), .clr(rst));  // open: load, D, carry
  Hex_Digit_Display hex_digit_display_1 (.value(counter_1_q));  // open: dp
endmodule
