// Logisim project 实验10_综合实验.circ as structural Verilog: 2 circuits, main circuit main
module main (
  input  a,
  input  b,
  input  c,
  input  d,
  input  e,
  input  f,
  input  g,
  input  h
);

  wire clock_1_out, x_1_out0, x_1_out1, x_1_out2, x_1_out3, x_1_out4, x_1_out_5, x_1_out_6, x_1_out_7;
  wire [3:0] counter_1_q;

  Clock clock_1 (.out(clock_1_out));
  Counter #(.width(4), .max('hf)) counter_1 (.Q(counter_1_q), .clk(clock_1_out));  // open: load, D, count, carry, clr
  Hex_Digit_Display hex_digit_display_1 (.value(counter_1_q));  // open: dp
  x x_1 (
    .in_0(counter_1_q[3]), .in_1(counter_1_q[2]), .in_2(counter_1_q[1]), .in_3(counter_1_q[0]),
    .out0(x_1_out0), .out1(x_1_out1), .out2(x_1_out2), .out3(x_1_out3), .out4(x_1_out4), .out_5(x_1_out_5),
    .out_6(x_1_out_6), .out_7(x_1_out_7));
  _7_Segment_Display u_7_segment_display_1 (
    .g(x_1_out3), .f(x_1_out2), .a(x_1_out1), .b(x_1_out0), .e(x_1_out4), .d(x_1_out_5), .c(x_1_out_6),
    .dp(x_1_out_7));
  _7_Segment_Display u_7_segment_display_2 (.g(d), .f(c), .a(b), .b(a), .e(e), .d(f), .c(g), .dp(h));
endmodule

module x (
  input  in_0,
  input  in_1,
  input  in_2,
  input  in_3,
  output out0,
  output out1,
  output out2,
  output out3,
  output out4,
  output out_5,
  output out_6,
  output out_7
);

  wire and_1_out, and_2_out, and_3_out, and_4_out, and_5_out, and_6_out, and_7_out, and_8_out, and_9_out,
       and_10_out, and_11_out, and_12_out, and_13_out, and_14_out, and_15_out, and_16_out, and_17_out,
       and_18_out, and_19_out, and_20_out, and_21_out, and_22_out, and_23_out, and_24_out, and_25_out,
       and_26_out, and_27_out, and_28_out, and_29_out, and_30_out, and_31_out, and_32_out, and_33_out,
       and_34_out, and_35_out, not_1_out, not_2_out, not_3_out, not_4_out, not_5_out, not_6_out, not_7_out,
       not_8_out, not_9_out, not_10_out, not_11_out, not_12_out, not_13_out, not_14_out, not_15_out,
       not_16_out, not_17_out, not_18_out, not_19_out, not_20_out, not_21_out, not_22_out, not_23_out,
       not_24_out, not_25_out, not_26_out, not_27_out, not_28_out, not_29_out, not_30_out, not_31_out,
       not_32_out, not_33_out, not_34_out, not_35_out, not_36_out, not_37_out, not_38_out, not_39_out,
       not_40_out, not_41_out, not_42_out, not_43_out, not_44_out, not_45_out;

  not not_1 (not_1_out, in_0);
  and and_1 (and_1_out, not_1_out, not_2_out);
  not not_2 (not_2_out, in_1);
  not not_3 (not_3_out, in_0);
  and and_2 (and_2_out, not_3_out, not_4_out, not_5_out);
  not not_4 (not_4_out, in_2);
  not not_5 (not_5_out, in_3);
  not not_6 (not_6_out, in_1);
  and and_3 (and_3_out, not_6_out, not_7_out);
  not not_7 (not_7_out, in_3);
  not not_8 (not_8_out, in_0);
  and and_4 (and_4_out, not_8_out, in_2, in_3);
  and and_5 (and_5_out, in_0, not_9_out, in_3);
  not not_9 (not_9_out, in_2);
  not not_10 (not_10_out, in_1);
  and and_6 (and_6_out, not_10_out, not_11_out);
  not not_11 (not_11_out, in_3);
  not not_12 (not_12_out, in_0);
  and and_7 (and_7_out, not_12_out, in_2);
  not not_13 (not_13_out, in_0);
  and and_8 (and_8_out, not_13_out, in_1, in_3);
  and and_9 (and_9_out, in_1, in_2);
  not not_14 (not_14_out, in_1);
  and and_10 (and_10_out, in_0, not_14_out, not_15_out);
  not not_15 (not_15_out, in_2);
  and and_11 (and_11_out, in_0, not_16_out);
  not not_16 (not_16_out, in_3);
  not not_17 (not_17_out, in_2);
  and and_12 (and_12_out, not_17_out, not_18_out);
  not not_18 (not_18_out, in_3);
  not not_19 (not_19_out, in_0);
  and and_13 (and_13_out, not_19_out, in_1, not_20_out);
  not not_20 (not_20_out, in_2);
  and and_14 (and_14_out, in_1, not_21_out);
  not not_21 (not_21_out, in_3);
  and and_15 (and_15_out, in_0, not_22_out);
  not not_22 (not_22_out, in_1);
  and and_16 (and_16_out, in_0, in_2);
  not not_23 (not_23_out, in_1);
  and and_17 (and_17_out, not_23_out, in_2);
  and and_18 (and_18_out, in_2, not_24_out);
  not not_24 (not_24_out, in_3);
  not not_25 (not_25_out, in_0);
  and and_19 (and_19_out, not_25_out, in_1, not_26_out);
  not not_26 (not_26_out, in_2);
  and and_20 (and_20_out, in_0, not_27_out);
  not not_27 (not_27_out, in_1);
  and and_21 (and_21_out, in_0, in_3);
  not not_28 (not_28_out, in_1);
  and and_22 (and_22_out, not_28_out, not_29_out);
  not not_29 (not_29_out, in_3);
  and and_23 (and_23_out, in_2, not_30_out);
  not not_30 (not_30_out, in_3);
  and and_24 (and_24_out, in_0, in_2);
  and and_25 (and_25_out, in_0, in_1);
  not not_31 (not_31_out, in_0);
  not not_32 (not_32_out, in_1);
  and and_26 (and_26_out, not_31_out, not_32_out, not_33_out);
  not not_33 (not_33_out, in_3);
  not not_34 (not_34_out, in_1);
  and and_27 (and_27_out, not_34_out, in_2, in_3);
  not not_35 (not_35_out, in_2);
  and and_28 (and_28_out, in_1, not_35_out, in_3);
  and and_29 (and_29_out, in_1, in_2, not_36_out);
  not not_36 (not_36_out, in_3);
  not not_37 (not_37_out, in_2);
  and and_30 (and_30_out, in_0, not_37_out, not_38_out);
  not not_38 (not_38_out, in_3);
  not not_39 (not_39_out, in_0);
  and and_31 (and_31_out, not_39_out, not_40_out);
  not not_40 (not_40_out, in_2);
  not not_41 (not_41_out, in_0);
  and and_32 (and_32_out, not_41_out, in_3);
  not not_42 (not_42_out, in_2);
  and and_33 (and_33_out, not_42_out, in_3);
  not not_43 (not_43_out, in_0);
  and and_34 (and_34_out, not_43_out, in_1);
  and and_35 (and_35_out, in_0, not_44_out);
  not not_44 (not_44_out, in_1);
  not not_45 (not_45_out, in_1);
  or or_1 (out0, and_1_out, and_2_out, and_3_out, and_4_out, and_5_out);
  or or_2 (out2, and_12_out, and_13_out, and_14_out, and_15_out, and_16_out);
  or or_3 (out3, and_17_out, and_18_out, and_19_out, and_20_out, and_21_out);
  or or_4 (out4, and_22_out, and_23_out, and_24_out, and_25_out);
  or or_5 (out_5, and_26_out, and_27_out, and_28_out, and_29_out, and_30_out);
  or or_6 (out_6, and_31_out, and_32_out, and_33_out, and_34_out, and_35_out);
  and and_36 (out_7, in_0, not_45_out, in_2, in_3);
  or or_7 (out1, and_6_out, and_7_out, and_8_out, and_9_out, and_10_out, and_11_out);
endmodule
